# Fritzing sketch LED_strip (saved by Fritzing 0.9.2b)

parts:
  Part1 = Arduino Uno (Rev3)
  NEOPIXEL1 = Neopixel Strip -- Black (30/m)

nets:
  N1: Part1.D8, NEOPIXEL1.Din
  5V: Part1.5V, NEOPIXEL1.+5V
  GND: Part1.GND, NEOPIXEL1.GND

custom parts:
  Neopixel Strip -- Black (30/m): These NeoPixel strips have 30 digitally-addressable pixel LEDs per meter and are very affordable and are only 12.5 mm wide, 10 mm if you remove the strip from the casing.
