# Fritzing sketch digit (saved by Fritzing 0.9.2b)
breadboards: 1

parts:
  R1 = Resistor [tolerance=±5% resistance=220 package=THT]
  U1 = 7-SEGMENT-DISPLAY-1_-RED [package=7-segment-1_pth]
  Part1 = Arduino Uno (Rev3)

nets:
  N1: R1.Pin_0, Part1.GND
  N2: R1.Pin_1, U1.G1, U1.G2
  N3: U1.E, Part1.D6_PWM
  N4: U1.D, Part1.D5_PWM
  N5: U1.C, Part1.D4
  N6: U1.B, Part1.D3_PWM
  N7: U1.A, Part1.D2
  N8: U1.F, Part1.D8
  N9: U1.G, Part1.D7
