# Fritzing sketch motion_detection (saved by Fritzing 0.9.2b)

parts:
  Part1 = Arduino Uno (Rev3)
  PIR1 = PIR sensor
  J1 = Basic Servo

nets:
  N1: Part1.D8, PIR1.SIG
  N2: Part1.D12/MISO, J1.pulse
  3V3: Part1.3V3, J1.vcc
  5V: Part1.5V, PIR1.VDD
  GND: Part1.GND, PIR1.GND, J1.gnd
