# Fritzing sketch photoresistor (saved by Fritzing 0.9.2b)
breadboards: 1

parts:
  R1 = Resistor [tolerance=±5% resistance=10k package=THT]
  Part1 = Arduino Uno (Rev3)
  R2 = PHOTOCELL [package=photocell]
  J1 = Piezo Speaker

nets:
  N1: R1.Pin_0, Part1.A0, R2.P$2
  N2: R1.Pin_1, Part1.GND, J1.pin1
  N3: Part1.D8, J1.pin2
  N4: Part1.5V, R2.P$1
